// Logisim project trab_sim_dados.circ as structural Verilog: 2 circuits, main circuit main
module main (
  input  A0,
  input  A1,
  input  A2,
  output L1,
  output L2,
  output L3,
  output L4,
  output L5,
  output L6,
  output L7
);

  DADO dado_1 (.A0(A0), .A1(A1), .A2(A2), .L1(L1), .L2(L2), .L3(L3), .L4(L4), .L5(L5), .L6(L6), .L7(L7));
endmodule

module DADO (
  input  A0,
  input  A1,
  input  A2,
  output L1,
  output L2,
  output L3,
  output L4,
  output L5,
  output L6,
  output L7
);

  wire and_2_out, and_3_out, not_1_out, not_2_out;

  not not_1 (not_1_out, A0);
  not not_2 (not_2_out, A1);
  or or_1 (L1, A1, A0);
  and and_1 (L3, A0, A1);
  and and_2 (and_2_out, not_1_out, A2);
  and and_3 (and_3_out, not_2_out, A2);
  or or_2 (L4, and_2_out, and_3_out);

  assign L2 = A0;
  assign L5 = L3;
  assign L6 = A0;
  assign L7 = L1;
endmodule
